// Logisim project lab2.circ as structural Verilog
module \生成电路  (
  input  I4,
  input  I3,
  input  I2,
  input  I1,
  output O4,
  output O3,
  output O2,
  output O1
);

  wire and_2_out, not_3_out, not_4_out;

  not not_1 (O4, I2);
  and and_1 (O3, I2, I1);
  not not_2 (O2, I3);
  not not_3 (not_3_out, I1);
  not not_4 (not_4_out, I4);
  and and_2 (and_2_out, not_4_out, I2);
  or or_1 (O1, not_3_out, and_2_out, I3);

  // Notes on the sheet:
  //   侯超群-PB21111618
endmodule

module \表达式生成电路  (
  input  i0,
  input  i1,
  input  i2,
  input  i3,
  input  i4,
  input  i5,
  input  i6,
  input  i7,
  output y0,
  output y1,
  output y2
);

  wire and_1_out, and_2_out, and_3_out, and_4_out, and_5_out, not_1_out, not_2_out, not_3_out, not_4_out,
       not_5_out, not_6_out, not_7_out, not_8_out, not_9_out, not_10_out;

  not not_1 (not_1_out, i6);
  not not_2 (not_2_out, i4);
  not not_3 (not_3_out, i6);
  not not_4 (not_4_out, i2);
  not not_5 (not_5_out, i4);
  not not_6 (not_6_out, i6);
  and and_1 (and_1_out, i3, not_7_out, not_8_out);
  not not_7 (not_7_out, i4);
  not not_8 (not_8_out, i5);
  and and_2 (and_2_out, i2, not_9_out, not_10_out);
  not not_9 (not_9_out, i4);
  not not_10 (not_10_out, i5);
  or or_1 (y2, i7, i6, i5, i4);
  and and_3 (and_3_out, i5, not_1_out);
  and and_4 (and_4_out, i3, not_2_out, not_3_out);
  and and_5 (and_5_out, i1, not_4_out, not_5_out, not_6_out);
  or or_2 (y1, i7, i6, and_1_out, and_2_out);
  or or_3 (y0, i7, and_3_out, and_4_out, and_5_out);
endmodule

module problem1 (
  input  Ci1,
  input  Ai,
  input  Bi,
  output Si,
  output Ci
);

  wire and_1_out, and_2_out, and_3_out, and_4_out, and_5_out, and_6_out, and_7_out, not_1_out, not_2_out,
       not_3_out, not_4_out, not_5_out, not_6_out;

  not not_1 (not_1_out, Ci1);
  not not_2 (not_2_out, Ai);
  not not_3 (not_3_out, Ci1);
  not not_4 (not_4_out, Bi);
  not not_5 (not_5_out, Ai);
  not not_6 (not_6_out, Bi);
  and and_1 (and_1_out, Ai, Bi);
  and and_2 (and_2_out, Ci1, Bi);
  and and_3 (and_3_out, Ci1, Ai);
  and and_4 (and_4_out, not_1_out, not_2_out, Bi);
  and and_5 (and_5_out, not_3_out, Ai, not_4_out);
  and and_6 (and_6_out, Ci1, not_5_out, not_6_out);
  and and_7 (and_7_out, Ci1, Ai, Bi);
  or or_1 (Ci, and_1_out, and_2_out, and_3_out);
  or or_2 (Si, and_4_out, and_5_out, and_6_out, and_7_out);

  // Notes on the sheet:
  //   侯超群-PB21111618
endmodule

module problem2 (
  input  G1,
  input  G2,
  input  G3,
  input  A2,
  input  A1,
  input  A0,
  output Y7,
  output Y6,
  output Y5,
  output Y4,
  output Y3,
  output Y2,
  output Y1,
  output Y0
);

  wire not_1_out, not_2_out, not_3_out, not_4_out, not_5_out, not_6_out, not_7_out, not_8_out, not_9_out,
       not_10_out, not_11_out, not_12_out, not_13_out, not_14_out, not_15_out, not_16_out, not_17_out,
       not_18_out, not_19_out, not_20_out;

  not not_1 (not_1_out, G1);
  not not_2 (not_2_out, A2);
  not not_3 (not_3_out, A1);
  not not_4 (not_4_out, A0);
  not not_5 (not_5_out, G1);
  not not_6 (not_6_out, A2);
  not not_7 (not_7_out, A1);
  not not_8 (not_8_out, G1);
  not not_9 (not_9_out, A2);
  not not_10 (not_10_out, A0);
  not not_11 (not_11_out, G1);
  not not_12 (not_12_out, A2);
  not not_13 (not_13_out, G1);
  not not_14 (not_14_out, A1);
  not not_15 (not_15_out, A0);
  not not_16 (not_16_out, G1);
  not not_17 (not_17_out, A1);
  not not_18 (not_18_out, G1);
  not not_19 (not_19_out, A0);
  not not_20 (not_20_out, G1);
  or or_1 (Y7, not_1_out, not_2_out, not_3_out, not_4_out, G3, G2);
  or or_2 (Y6, not_5_out, not_6_out, not_7_out, A0, G3, G2);
  or or_3 (Y5, not_8_out, not_9_out, not_10_out, A1, G3, G2);
  or or_4 (Y4, not_11_out, not_12_out, A0, A1, G3, G2);
  or or_5 (Y3, not_13_out, not_14_out, not_15_out, A2, G3, G2);
  or or_6 (Y2, not_16_out, not_17_out, A0, A2, G3, G2);
  or or_7 (Y1, not_18_out, not_19_out, A1, A2, G3, G2);
  or or_8 (Y0, not_20_out, A0, A1, A2, G3, G2);

  // Notes on the sheet:
  //   侯超群-PB21111618
endmodule

module problem2_new (
  input  G1,
  input  G2,
  input  G3,
  input  A2,
  input  A1,
  input  A0,
  output Y7,
  output Y6,
  output Y5,
  output Y4,
  output Y3,
  output Y2,
  output Y1,
  output Y0
);

  wire not_1_out, not_2_out, not_3_out, not_4_out, not_5_out, not_6_out, not_7_out, not_8_out, not_9_out,
       not_10_out, not_11_out, not_12_out, not_13_out, not_14_out, not_15_out, not_16_out, not_17_out,
       not_18_out, not_19_out, not_20_out, not_21_out, not_22_out, not_23_out, not_24_out, not_25_out,
       not_26_out, not_27_out, not_28_out;

  not not_1 (not_1_out, G2);
  not not_2 (not_2_out, G3);
  not not_3 (not_3_out, G2);
  not not_4 (not_4_out, G3);
  not not_5 (not_5_out, A0);
  not not_6 (not_6_out, G2);
  not not_7 (not_7_out, G3);
  not not_8 (not_8_out, A1);
  not not_9 (not_9_out, G2);
  not not_10 (not_10_out, G3);
  not not_11 (not_11_out, A1);
  not not_12 (not_12_out, A0);
  not not_13 (not_13_out, G2);
  not not_14 (not_14_out, G3);
  not not_15 (not_15_out, A2);
  not not_16 (not_16_out, G2);
  not not_17 (not_17_out, G3);
  not not_18 (not_18_out, A2);
  not not_19 (not_19_out, A0);
  not not_20 (not_20_out, G2);
  not not_21 (not_21_out, G3);
  not not_22 (not_22_out, A2);
  not not_23 (not_23_out, A1);
  not not_24 (not_24_out, G2);
  not not_25 (not_25_out, G3);
  not not_26 (not_26_out, A2);
  not not_27 (not_27_out, A1);
  not not_28 (not_28_out, A0);
  nand nand_1 (Y7, G1, not_1_out, not_2_out, A2, A1, A0);
  nand nand_2 (Y6, G1, not_3_out, not_4_out, A2, A1, not_5_out);
  nand nand_3 (Y5, G1, not_6_out, not_7_out, A2, not_8_out, A0);
  nand nand_4 (Y4, G1, not_9_out, not_10_out, A2, not_11_out, not_12_out);
  nand nand_5 (Y3, G1, not_13_out, not_14_out, not_15_out, A1, A0);
  nand nand_6 (Y2, G1, not_16_out, not_17_out, not_18_out, A1, not_19_out);
  nand nand_7 (Y1, G1, not_20_out, not_21_out, not_22_out, not_23_out, A0);
  nand nand_8 (Y0, G1, not_24_out, not_25_out, not_26_out, not_27_out, not_28_out);

  // Notes on the sheet:
  //   侯超群-PB21111618
endmodule

module choose2_1 (
  input  sel,
  input  a,
  input  b,
  output out
);

  wire and_1_out, and_2_out, not_1_out;

  not not_1 (not_1_out, sel);
  and and_1 (and_1_out, not_1_out, a);
  and and_2 (and_2_out, sel, b);
  or or_1 (out, and_1_out, and_2_out);

  // Notes on the sheet:
  //   侯超群-PB21111618
endmodule

module \表达式生成电路_原  (
  input  i0,
  input  i0_2,
  input  i1,
  input  i1_2,
  input  i2,
  input  i2_2,
  input  i3,
  input  i3_2,
  input  i4,
  input  i4_2,
  input  i5,
  input  i5_2,
  input  i6,
  input  i6_2,
  input  i7,
  input  i7_2,
  input  i0_3,
  input  i1_3,
  input  i2_3,
  input  i3_3,
  input  i4_3,
  input  i5_3,
  input  i6_3,
  input  i7_3,
  output y0,
  output y0_2,
  output y1,
  output y2,
  output y1_2,
  output y0_3,
  output y2_2,
  output y1_3,
  output y2_3
);

  wire and_1_out, and_2_out, and_3_out, and_4_out, and_5_out, and_6_out, and_7_out, and_8_out, and_9_out,
       and_10_out, and_11_out, and_12_out, and_13_out, and_14_out, not_1_out, not_2_out, not_3_out,
       not_4_out, not_5_out, not_6_out, not_7_out, not_8_out, not_9_out, not_10_out, not_11_out, not_12_out,
       not_13_out, not_14_out, not_15_out, not_16_out, not_17_out, not_18_out, not_19_out, not_20_out,
       not_21_out, not_22_out, not_23_out, not_24_out, not_25_out, not_26_out, not_27_out, not_28_out,
       not_29_out, not_30_out, not_31_out, not_32_out, not_33_out, not_34_out, not_35_out, not_36_out,
       not_37_out, not_38_out, not_39_out, not_40_out, not_41_out, not_42_out, not_43_out, or_5_out,
       or_6_out, or_7_out, or_10_out, or_11_out, or_12_out, or_13_out;

  not not_1 (not_1_out, i7_2);
  not not_2 (not_2_out, i6);
  not not_3 (not_3_out, i7_2);
  not not_4 (not_4_out, i6);
  not not_5 (not_5_out, i5);
  not not_6 (not_6_out, i4);
  not not_7 (not_7_out, i7_2);
  not not_8 (not_8_out, i6);
  not not_9 (not_9_out, i5);
  not not_10 (not_10_out, i4);
  not not_11 (not_11_out, i3);
  not not_12 (not_12_out, i2);
  not not_13 (not_13_out, i7_2);
  not not_14 (not_14_out, i7_2);
  not not_15 (not_15_out, i6);
  not not_16 (not_16_out, i5);
  not not_17 (not_17_out, i4);
  not not_18 (not_18_out, i7_2);
  not not_19 (not_19_out, i6);
  not not_20 (not_20_out, i5);
  not not_21 (not_21_out, i4);
  not not_22 (not_22_out, i3);
  not not_23 (not_23_out, i7_2);
  not not_24 (not_24_out, i7_2);
  not not_25 (not_25_out, i6);
  not not_26 (not_26_out, i7_2);
  not not_27 (not_27_out, i6);
  not not_28 (not_28_out, i5);
  and and_1 (and_1_out, not_1_out, not_2_out, i5);
  and and_2 (and_2_out, not_3_out, not_4_out, not_5_out, not_6_out, i3);
  and and_3 (and_3_out, not_7_out, not_8_out, not_9_out, not_10_out, not_11_out, not_12_out, i1);
  and and_4 (and_4_out, not_13_out, i6);
  and and_5 (and_5_out, not_14_out, not_15_out, not_16_out, not_17_out, i3);
  and and_6 (and_6_out, not_18_out, not_19_out, not_20_out, not_21_out, not_22_out, i2);
  and and_7 (and_7_out, not_23_out, i6);
  and and_8 (and_8_out, not_24_out, not_25_out, i5);
  and and_9 (and_9_out, not_26_out, not_27_out, not_28_out, i4);
  or or_1 (y0_2, i7_2, and_1_out, and_2_out, and_3_out);
  or or_2 (y1_2, i7_2, and_4_out, and_5_out, and_6_out);
  or or_3 (y2_2, i7_2, and_7_out, and_8_out, and_9_out);
  not not_29 (not_29_out, i2_2);
  not not_30 (not_30_out, i2_2);
  not not_31 (not_31_out, i2_2);
  not not_32 (not_32_out, i2_2);
  not not_33 (not_33_out, i2_2);
  not not_34 (not_34_out, i2_2);
  and and_10 (and_10_out, i3_2, not_35_out, not_36_out);
  not not_35 (not_35_out, i2_2);
  not not_36 (not_36_out, i2_2);
  and and_11 (and_11_out, i2_2, not_37_out, not_38_out);
  not not_37 (not_37_out, i2_2);
  not not_38 (not_38_out, i2_2);
  or or_4 (y2, i2_2, i2_2, i2_2, i2_2);
  not not_39 (not_39_out, i6_3);
  not not_40 (not_40_out, i4_3);
  not not_41 (not_41_out, i2_3);
  or or_5 (or_5_out, i2_3, i3_3, i6_3, i7_3);
  not not_42 (not_42_out, i5_3);
  or or_6 (or_6_out, not_42_out, i6_3, i7_3);
  not not_43 (not_43_out, i4_3);
  or or_7 (or_7_out, not_43_out, i6_3, i7_3);
  or or_8 (y2_3, i4_3, i5_3, i6_3, i7_3);
  and and_12 (and_12_out, i2_2, not_29_out);
  and and_13 (and_13_out, i3_2, not_30_out, not_31_out);
  and and_14 (and_14_out, i1_2, not_32_out, not_33_out, not_34_out);
  or or_9 (y1, i2_2, i2_2, and_10_out, and_11_out);
  or or_10 (or_10_out, i1_3, i3_3, i5_3, i7_3);
  or or_11 (or_11_out, not_39_out, i7_3);
  or or_12 (or_12_out, not_40_out, i5_3, i7_3);
  or or_13 (or_13_out, not_41_out, i3_3, i5_3, i7_3);
  and and_15 (y1_3, or_5_out, or_6_out, or_7_out);
  or or_14 (y0, i2_2, and_12_out, and_13_out, and_14_out);
  and and_16 (y0_3, or_10_out, or_11_out, or_12_out, or_13_out);

  assign i4_2 = i2_2;
  assign i5_2 = i2_2;
  assign i6_2 = i2_2;
  assign i7 = i2_2;

  // Notes on the sheet:
  //   侯超群-PB21111618
endmodule

module choose4_1 (
  input  sel0,
  input  sel1,
  input  a,
  input  b,
  input  c,
  input  d,
  output out
);

  wire choose2_1_1_out, choose2_1_2_out;

  choose2_1 choose2_1_1 (.sel(sel1), .a(a), .b(b), .out(choose2_1_1_out));
  choose2_1 choose2_1_2 (.sel(sel1), .a(c), .b(d), .out(choose2_1_2_out));
  choose2_1 choose2_1_3 (.sel(sel0), .a(choose2_1_1_out), .b(choose2_1_2_out), .out(out));

  // Notes on the sheet:
  //   侯超群-PB21111618
endmodule
