// Logisim project lab3.circ as structural Verilog
module \SR锁存器  (
  input  R,
  input  S,
  output Q,
  output nQ
);

  nor nor_1 (Q, R, nQ);
  nor nor_2 (nQ, Q, S);
endmodule

module \D锁存器  (
  input  CLK,
  input  D,
  output Q,
  output nQ
);

  wire and_1_out, and_2_out, not_1_out;

  not not_1 (not_1_out, D);
  and and_1 (and_1_out, CLK, not_1_out);
  and and_2 (and_2_out, CLK, D);
  \SR锁存器  \sr锁存器_1  (.R(and_1_out), .S(and_2_out), .Q(Q), .nQ(nQ));
endmodule

module \D触发器  (
  input  CLK,
  input  D,
  output Q,
  output nQ
);

  wire \d锁存器_1_q , not_1_out;

  not not_1 (not_1_out, CLK);
  \D锁存器  \d锁存器_1  (.D(D), .Q(\d锁存器_1_q ), .CLK(not_1_out));  // open: nQ
  \D锁存器  \d锁存器_2  (.D(\d锁存器_1_q ), .Q(Q), .nQ(nQ), .CLK(CLK));
endmodule

module \寄存器  (
  input  [3:0] D_IN,
  input  CLK,
  input  RST_N,
  output [3:0] D_OUT
);

  wire and_1_out, and_2_out, and_3_out, and_4_out;

  and and_1 (and_1_out, RST_N, D_IN[3]);
  and and_2 (and_2_out, RST_N, D_IN[2]);
  and and_3 (and_3_out, RST_N, D_IN[1]);
  and and_4 (and_4_out, RST_N, D_IN[0]);
  \D触发器  \d触发器_1  (.D(and_1_out), .Q(D_OUT[3]), .CLK(CLK));  // open: nQ
  \D触发器  \d触发器_2  (.D(and_2_out), .Q(D_OUT[2]), .CLK(CLK));  // open: nQ
  \D触发器  \d触发器_3  (.D(and_3_out), .Q(D_OUT[1]), .CLK(CLK));  // open: nQ
  \D触发器  \d触发器_4  (.D(and_4_out), .Q(D_OUT[0]), .CLK(CLK));  // open: nQ
endmodule

module problem1 (
  input  S_prime,
  input  R_prime,
  output Q,
  output nQ
);

  nand nand_1 (Q, S_prime, nQ);
  nand nand_2 (nQ, Q, R_prime);

  // Notes on the sheet:
  //                                PB21111618_侯超群
endmodule

module problem2 (
  input  D,
  input  nRST,
  output Q,
  output nQ
);

  wire and_1_out, CLK_out, \d锁存器_1_q , not_1_out;

  Clock CLK (.out(CLK_out));
  not not_1 (not_1_out, CLK_out);
  and and_1 (and_1_out, D, nRST);
  \D锁存器  \d锁存器_1  (.D(and_1_out), .Q(\d锁存器_1_q ), .CLK(not_1_out));  // open: nQ
  \D锁存器  \d锁存器_2  (.D(\d锁存器_1_q ), .Q(Q), .nQ(nQ), .CLK(CLK_out));

  // Notes on the sheet:
  //                                PB21111618_侯超群
endmodule

module problem3 (
  input  nRST,
  input  CLK,
  input  D,
  output Q,
  output nQ
);

  wire \d锁存器_1_q , \d锁存器_2_nq , \d锁存器_2_q , not_1_out, not_2_out;

  not not_1 (not_1_out, CLK);
  \D锁存器  \d锁存器_1  (.D(D), .Q(\d锁存器_1_q ), .CLK(not_1_out));  // open: nQ
  \D锁存器  \d锁存器_2  (.D(\d锁存器_1_q ), .Q(\d锁存器_2_q ), .nQ(\d锁存器_2_nq ), .CLK(CLK));
  not not_2 (not_2_out, nRST);
  and and_1 (Q, nRST, \d锁存器_2_q );
  or or_1 (nQ, not_2_out, \d锁存器_2_nq );

  // Notes on the sheet:
  //                                PB21111618_侯超群
endmodule

module problem3_4bit (
  input  RST_N,
  input  [3:0] D_IN,
  input  CLK,
  output [3:0] D_OUT
);

  problem3 problem3_1 (.nRST(RST_N), .D(D_IN[0]), .Q(D_OUT[0]), .CLK(CLK));  // open: nQ
  problem3 problem3_2 (.nRST(RST_N), .D(D_IN[1]), .Q(D_OUT[1]), .CLK(CLK));  // open: nQ
  problem3 problem3_3 (.nRST(RST_N), .D(D_IN[2]), .Q(D_OUT[2]), .CLK(CLK));  // open: nQ
  problem3 problem3_4 (.nRST(RST_N), .D(D_IN[3]), .Q(D_OUT[3]), .CLK(CLK));  // open: nQ

  // Notes on the sheet:
  //                                PB21111618_侯超群
endmodule

module problem3_coutnum (
  input  RST_N,
  output [3:0] out_2
);

  wire clock_1_out;
  wire [3:0] adder_1_out;

  Adder #(.width(4)) adder_1 (.a(4'b0001), .b(out_2), .out(adder_1_out), .cin(1'b0));  // open: cout
  Clock clock_1 (.out(clock_1_out));
  problem3_4bit problem3_4bit_1 (.RST_N(RST_N), .D_IN(adder_1_out), .D_OUT(out_2), .CLK(clock_1_out));

  // Notes on the sheet:
  //                                PB21111618_侯超群
endmodule

module problem4 (
  input  RST_N,
  output [3:0] out_2
);

  wire CLK_out;
  wire [3:0] or_1_out, subtractor_1_out, \寄存器_1_d_out ;
  wire [3:3] not_1_out;

  Subtractor #(.width(4)) subtractor_1 (.a(out_2), .b(4'b0001), .out(subtractor_1_out), .bin(1'b0));  // open: bout
  Clock CLK (.out(CLK_out));
  not not_1 (not_1_out[3], RST_N);
  \寄存器  \u_寄存器_1  (.D_IN(subtractor_1_out), .RST_N(RST_N), .D_OUT(\寄存器_1_d_out ), .CLK(CLK_out));
  assign or_1_out = \寄存器_1_d_out  | {4{not_1_out[3]}};  // OR_Gate or_1, 4 bits wide
  choose2_1_4bit choose2_1_4bit_1 (.\input (or_1_out), .compare(4'b1001), .\output (out_2));

  // Notes on the sheet:
  //                                PB21111618_侯超群
endmodule

module choose2_1_4bit (
  input  [3:0] \input ,
  input  [3:0] compare,
  output [3:0] \output 
);

  wire [3:0] and_1_out, and_2_out, not_1_out;
  wire [3:3] or_1_out;

  or or_1 (or_1_out[3], ~\input [0], ~\input [1], ~\input [2], ~\input [3]);  // OR_Gate
  assign not_1_out = ~{4{or_1_out[3]}};  // NOT_Gate not_1, 4 bits wide
  assign and_1_out = {4{or_1_out[3]}} & \input ;  // AND_Gate and_1, 4 bits wide
  assign and_2_out = not_1_out & compare;  // AND_Gate and_2, 4 bits wide
  assign \output  = and_1_out | and_2_out;  // OR_Gate or_2, 4 bits wide

  // Notes on the sheet:
  //                                PB21111618_侯超群
endmodule

module problem5 (
  input  D,
  input  nRST,
  output Q,
  output nQ
);

  wire and_1_out, CLK_out, \d锁存器_1_q , not_1_out, not_2_out;

  Clock CLK (.out(CLK_out));
  not not_1 (not_1_out, nRST);
  not not_2 (not_2_out, CLK_out);
  and and_1 (and_1_out, D, not_1_out);
  \D锁存器  \d锁存器_1  (.D(and_1_out), .Q(\d锁存器_1_q ), .CLK(not_2_out));  // open: nQ
  \D锁存器  \d锁存器_2  (.D(\d锁存器_1_q ), .Q(Q), .nQ(nQ), .CLK(CLK_out));

  // Notes on the sheet:
  //                                PB21111618_侯超群
endmodule
