// Logisim project lab8.circ as structural Verilog: 3 circuits, main circuit main
module main (
);

  wire [1:0] multiplexer_1_out, multiplexer_2_out, undriven;

  Multiplexer #(.select(2), .width(2)) multiplexer_1 (
    .in0(2'b01), .in1(2'b10), .in2(2'b00), .in3(2'b00), .out(multiplexer_1_out), .sel(undriven));  // open: en
  Multiplexer #(.width(2)) multiplexer_2 (
    .in0(undriven), .in1(multiplexer_1_out), .out(multiplexer_2_out));  // open: sel, en
endmodule

module problem2 (
  input  in_1,
  input  rst,
  output [3:0] out_3
);

  wire and_2_out, and_3_out, clock_1_out, d_ff_1_q, d_ff_2_q, not_2_out, not_3_out;
  wire [0:0] or_1_out;
  wire [3:0] adder_1_out, n4bitreg_1_d_out;
  wire [3:3] not_1_out;

  Clock clock_1 (.out(clock_1_out));
  not not_1 (not_1_out[3], rst);
  D_Flip_Flop d_ff_1 (.clk(clock_1_out), .D(in_1), .Q(d_ff_1_q));  // open: Qn, preset, en, reset
  Adder #(.width(4)) adder_1 (.a({3'b000, or_1_out[0]}), .b(out_3), .out(adder_1_out), .cin(1'b0));  // open: cout
  D_Flip_Flop d_ff_2 (.clk(clock_1_out), .D(d_ff_1_q), .Q(d_ff_2_q));  // open: Qn, preset, en, reset
  _4bitreg u_4bitreg_1 (.D_IN(adder_1_out), .CLK(clock_1_out), .D_OUT(n4bitreg_1_d_out));
  not not_2 (not_2_out, d_ff_2_q);
  not not_3 (not_3_out, d_ff_1_q);
  assign out_3 = n4bitreg_1_d_out & {4{not_1_out[3]}};  // AND_Gate and_1, 4 bits wide
  and and_2 (and_2_out, not_2_out, d_ff_1_q);
  and and_3 (and_3_out, d_ff_2_q, not_3_out);
  or or_1 (or_1_out[0], and_2_out, and_3_out);

  // Notes on the sheet:
  //   PB21111618-侯超群
endmodule

module _4bitreg (
  input  [3:0] D_IN,
  input  CLK,
  output [3:0] D_OUT
);

  D_Flip_Flop d_ff_1 (.clk(CLK), .D(D_IN[0]), .Q(D_OUT[0]));  // open: Qn, preset, en, reset
  D_Flip_Flop d_ff_2 (.clk(CLK), .D(D_IN[1]), .Q(D_OUT[1]));  // open: Qn, preset, en, reset
  D_Flip_Flop d_ff_3 (.clk(CLK), .D(D_IN[2]), .Q(D_OUT[2]));  // open: Qn, preset, en, reset
  D_Flip_Flop d_ff_4 (.clk(CLK), .D(D_IN[3]), .Q(D_OUT[3]));  // open: Qn, preset, en, reset

  // Notes on the sheet:
  //                                PB21111618_侯超群
endmodule
